# Fritzing sketch DesignSchematicWiring (saved by Fritzing 0.9.3b)

parts:
  U1 = ESP8266 NodeMCU LoLin base
  A1 = MQ-2 breakout
  A2 = BBAA100043
  buz1 = Piezo Buzzer
  DHT1 = Humidity and Temperature Sensor DHT11

nets:
  VCC: U1.3V1-0, U1.3V3-2, U1.3V3-3, U1.3V4, A1.VCC, DHT1.Vcc
  N1: U1.D0-0, U1.D0-3, A2.pin3
  N2: U1.D1-3, DHT1.Data-signal
  N3: U1.D2-0, U1.D2-3, A2.pin1
  GND6: U1.GND2-3, U1.GND3-0, U1.GND3-2, U1.GND3-3, U1.GND6, U1.GND8-4, A1.GND, A2.pin4, buz1.pin_1, DHT1.GND_2
  N4: U1.D7-0, U1.D7-3, buz1.pin_2
  N5: U1.A0, A1.AO

custom parts:
  ESP8266 NodeMCU LoLin base: ESP8266 based NodeMCU Base
  MQ-2 breakout: MQ-2 gas sensor
  BBAA100043: BBAA100043 traffic light module.
  Piezo Buzzer: Part from https://www.nutsvolts.com/magazine/article/november2012_SmileysWorkshop modified to be .3 in spacing to match the adafruit buzzer 5V breadboard friendly part.
  Humidity and Temperature Sensor DHT11: Digital relative humidity & temperature sensor DHT11
